// Logisim project cpu.circ as structural Verilog: 4 circuits, main circuit main
module main (
  input  [31:0] INSTRUCTION,
  input  CLOCK,
  output [31:0] FETCH_ADDRESS,
  output [31:0] s0_Value,
  output [31:0] s1_Value,
  output [31:0] s2_Value,
  output [31:0] ra_Value,
  output [31:0] sp_Value
);

  wire ALUsrc, ExtOp, main_3_p1, main_3_p2, main_3_p4, memToReg, MemWrite, RegDst, RegWrite;
  wire [4:0] multiplexer_1_out;
  wire [31:0] adder_1_out, aluResult, bit_extender_1_out, bit_extender_2_out, memResult, multiplexer_2_out,
       multiplexer_3_out, PC_q, writeData, x, y;

  Register #(.width(32)) PC (.D(adder_1_out), .Q(PC_q), .clk(CLOCK));  // open: en, clr
  Adder #(.width(32)) adder_1 (.a(PC_q), .b(32'h4), .out(adder_1_out));  // open: cin, cout
  control control_1 (
    .in_1(INSTRUCTION[31:26]), .RegDst(RegDst), .ALUSrc(ALUsrc), .MemToReg(memToReg), .RegWrite(RegWrite),
    .MemWrite(MemWrite), .ExtOp(ExtOp));  // open: nPC_se, jump, branch
  Multiplexer #(.width(5)) multiplexer_1 (
    .in0(INSTRUCTION[20:16]), .in1(INSTRUCTION[15:11]), .out(multiplexer_1_out), .sel(RegDst));  // open: en
  assign bit_extender_1_out = {{16{1'b0}}, INSTRUCTION[15:0]};  // Bit_Extender bit_extender_1
  assign bit_extender_2_out = {{16{INSTRUCTION[15]}}, INSTRUCTION[15:0]};  // Bit_Extender bit_extender_2
  regfile_main main_1 (
    .Read_Register_1(INSTRUCTION[25:21]), .Read_Register_2(INSTRUCTION[20:16]),
    .Write_Register(multiplexer_1_out), .Write_Data(writeData), .Write_Enable(RegWrite), .Clock(CLOCK),
    .Read_Data_1(x), .Read_Data_2(y), .s0_Value(s0_Value), .s1_Value(s1_Value), .s2_Value(s2_Value),
    .ra_Value(ra_Value), .sp_Value(sp_Value));
  Multiplexer #(.width(32)) multiplexer_2 (
    .in0(bit_extender_1_out), .in1(bit_extender_2_out), .out(multiplexer_2_out), .sel(ExtOp));  // open: en
  Multiplexer #(.width(32)) multiplexer_3 (
    .in0(y), .in1(multiplexer_2_out), .out(multiplexer_3_out), .sel(ALUsrc));  // open: en
  alu_main main_2 (.X(x), .Result(aluResult), .Y(multiplexer_3_out));  // open: Switch, Equal, Signed_Overflow
  // mem_main main_3: pin names not known; wires that end beside it: main_3_p1, main_3_p2, main_3_p2, main_3_p4, aluResult, y, MemWrite, CLOCK, memResult
  Multiplexer #(.width(32)) multiplexer_4 (
    .in0(memResult), .in1(aluResult), .out(writeData), .sel(memToReg));  // open: en

  // Other names for the same wires on the sheet: clk = CLOCK; fetch_addr[31:0] = FETCH_ADDRESS;
  //   imm[15:0] = INSTRUCTION[15:0]; rd[4:0] = INSTRUCTION[15:11]; rt[4:0] = INSTRUCTION[20:16];
  //   rs[4:0] = INSTRUCTION[25:21]; ra[31:0] = ra_Value; s0[31:0] = s0_Value; s1[31:0] = s1_Value;
  //   s2[31:0] = s2_Value; sp[31:0] = sp_Value

  // Notes on the sheet:
  //   Output
  //   These are outputs/inputs from run.circ
  //   Inputs
  //   These are DEBUG/TEST outputs from your circuit.
endmodule

module control (
  input  [5:0] in_1,
  output RegDst,
  output ALUSrc,
  output MemToReg,
  output RegWrite,
  output MemWrite,
  output nPC_se,
  output ExtOp,
  output jump,
  output branch
);

  wire [8:0] multiplexer_1_out, multiplexer_2_out;

  Multiplexer #(.select(4), .width(9)) multiplexer_1 (
    .in0(9'h9), .in2(9'ha0), .in3(9'ha0), .in4(9'h20), .in5(9'h20), .in8(9'h4a), .in9(9'h4a), .in10(9'h4a),
    .in11(9'h4a), .in12(9'ha), .in13(9'ha), .out(multiplexer_1_out), .sel(in_1[3:0]));  // open: in1, in6, in7, in14, in15, en
  Multiplexer #(.width(9)) multiplexer_2 (
    .in0(9'h4e), .in1(9'h52), .out(multiplexer_2_out), .sel(in_1[3]));  // open: en
  Multiplexer #(.width(9)) multiplexer_3 (
    .in0(multiplexer_1_out), .in1(multiplexer_2_out),
    .out({branch, jump, ExtOp, nPC_se, MemWrite, RegWrite, MemToReg, ALUSrc, RegDst}), .sel(in_1[5]));  // open: en

  // Other names for the same wires on the sheet: nPC_sel = nPC_se; _31_26[5:0] = in_1; lsb[3:0] = in_1[3:0];
  //   msb = in_1[5]
endmodule

module ALUcontrol (
  input  [5:0] funccode,
  input  [5:0] opcode
);

  wire comparator_1_eq, comparator_2_eq;
  wire [3:0] add;

  Comparator #(.width(6)) comparator_1 (.a(6'b100000), .b(funccode), .eq(comparator_1_eq));  // open: gt, lt
  Comparator #(.width(6)) comparator_2 (.a({6{1'b0}}), .b(opcode), .eq(comparator_2_eq));  // open: gt, lt
  Multiplexer #(.width(4)) multiplexer_1 (.in1(4'b0101), .out(add), .sel(comparator_1_eq));  // open: in0, en
  Multiplexer #(.width(6)) multiplexer_2 (.sel(comparator_2_eq));  // open: in0, in1, out, en
  Multiplexer #(.select(4), .width(4)) multiplexer_3 ();  // open: in0, in1, in2, in3, in4, in5, in6, in7, in8, in9, in10, in11, in12, in13, in14, in15, out, sel, en

  // Other names for the same wires on the sheet: funcode[5:0] = funccode
endmodule

module ControlUnit (
  input  [5:0] opcode
);

  wire nop0, nop1, nop2, nop3, nop4, nop5;

  not not_1 (nop5, opcode[5]);
  not not_2 (nop3, opcode[3]);
  not not_3 (nop4, opcode[4]);
  not not_4 (nop2, opcode[2]);
  not not_5 (nop1, opcode[1]);
  not not_6 (nop0, opcode[0]);

  // Other names for the same wires on the sheet: op0 = opcode[0]; op1 = opcode[1]; op2 = opcode[2]; op3 = opcode[3];
  //   op4 = opcode[4]; op5 = opcode[5]
endmodule
